# Fritzing sketch Schematic (saved by Fritzing 0.9.2b)
breadboards: 1

parts:
  IC1 = L293D [package=THT]
  Part2 = Lithium Ion Polymer Battery 3.7v 1200mAh [part_number=258]
  Part3 = Lithium Ion Polymer Battery 3.7v 1200mAh [part_number=258]
  M1 = DC Motor
  M2 = DC Motor [part_number="241                 }\n"]
  Part4 = HC-SR04
  Part1 = Arduino Uno (Rev3)
  R8 = Photocell (LDR) [package=THT]
  R9 = Resistor [tolerance=±5% resistance=10k package=THT]
  Part5 = HC-SR04

nets:
  VCC: IC1.Enable_1, IC1.Enable_2, IC1.+V, Part4.VCC, Part1.5V, R9.Pin_1, Part5.VCC
  N1: IC1.In_1, Part1.D6_PWM
  N2: IC1.Out_1_(_Controlled_by_Enable_1_), M2.pin_2
  GND: IC1.0V, Part3.negative, Part4.GND, Part1.GND, R8.pin_0, Part5.GND
  N3: IC1.Out_2_(_Controlled_by_Enable_1_), M2.pin_1
  N4: IC1.In_2, Part1.D7
  N5: IC1.+Vmotor, Part2.positive
  N6: IC1.In_3, Part1.D9_PWM
  N7: IC1.Out_3_(_Controlled_by_Enable_2_), M1.pin_1
  N8: IC1.Out_4_(_Controlled_by_Enable_2_), M1.pin_2
  N9: IC1.In_4, Part1.D10_PWM/SS
  N10: Part2.negative, Part3.positive
  N11: Part4.Trig, Part1.D3_PWM
  N12: Part4.Echo, Part1.D4
  N13: Part1.A0, R8.pin_1, R9.Pin_0
  N14: Part1.D12/MISO, Part5.Trig
  N15: Part1.D13/SCK, Part5.Echo

custom parts:
  Lithium Ion Polymer Battery 3.7v 1200mAh: Lithium ion polymer (also known as 'lipo' or 'lipoly') batteries are thin, light and powerful. The output ranges from 4.2V when completely charged to 3.7V. This battery has a capacity of 1200mAh for a total of about 4.5 Wh. The batteries come pre-attached with a genuine 2-pin JST-PH connector as shown and include the necessary protection circuitry.
  HC-SR04: Ultrasonic sensor.

// code stored in the sketch: Sumobot.ino
/********************************************
* Vincent Macri, David White, Rian Waterson *
* Mr. Wong                                  *
* 2017-11-09                                *
* Sumobot program.                          *
*********************************************/
// Define ultrasonic sensor pin numbers.
#define FRONT_TRIGGER 12
#define FRONT_ECHO 13
#define BACK_TRIGGER 3
#define BACK_ECHO 4

// Define LDR pins.
#define LDR_FRONT_LEFT A0
#define LDR_FRONT_RIGHT A1
#define LDR_BACK_LEFT A2
#define LDR_BACK_RIGHT A3

// Define motor pin numbers.
#define LEFT_FORWARD 9 // The pin to move the left motor forwards.
#define LEFT_BACKWARD 10 // The pin to move the left motor forwards.
#define RIGHT_FORWARD 6 // The pin to move the left motor forwards.
#define RIGHT_BACKWARD 7 // The pin to move the left motor forwards.

// Define constants.
#define SPEED_OF_SOUND 0.03434 // Speed of sound as STP in cm per microsecond.

// Variables for LDRs.
int frontLeftLight, frontRightLight, backLeftLight, backRightLight;

// Variables for distance tracking.

// The ultrasonic sensor reading.
double frontDistance, backDistance;

// Define thresholds.
#define DISTANCE_THRESHOLD 50
#define LDR_THRESHOLD 550

// Setup the program.
void setup() {
	// Setup the ultrasonic sensors.
	pinMode(FRONT_TRIGGER, OUTPUT); // Set the trigger pin as an output.
	pinMode(FRONT_ECHO, INPUT); // Set the echo pin as an input.
	pinMode(BACK_TRIGGER, OUTPUT); // Set the trigger pin as an output.
	pinMode(BACK_ECHO, INPUT); // Set the echo pin as an input.

	// Setup the motors.
	pinMode(LEFT_FORWARD, OUTPUT);
	pinMode(LEFT_BACKWARD, OUTPUT);
	pinMode(RIGHT_FORWARD, OUTPUT);
	pinMode(RIGHT_BACKWARD, OUTPUT);

	Serial.begin(9600); // Start the serial communication.
}

// Read the LDR sensor.
void readLDR() {
	frontLeftLight = analogRead(LDR_FRONT_LEFT);
	frontRightLight = analogRead(LDR_FRONT_RIGHT);
	backLeftLight = analogRead(LDR_BACK_LEFT);
	backRightLight = analogRead(LDR_BACK_RIGHT);
}

// Read the front ultrasonic sensor.
void readFrontUltrasonic() {
	// Clear the trigger pin.
	digitalWrite(FRONT_TRIGGER, LOW);
	delayMicroseconds(2);

	// Set the trigger pin on HIGH state for 10 micro seconds.
	digitalWrite(FRONT_TRIGGER, HIGH);
	delayMicroseconds(10);
	digitalWrite(FRONT_TRIGGER, LOW);

	// Read the echo pin.
	long duration = pulseIn(FRONT_ECHO, HIGH); // Sound wave travel time in microseconds.

	frontDistance = duration * SPEED_OF_SOUND / 2.0;
}

// Read the back ultrasonic sensor.
void readBackUltrasonic() {
	// Clear the trigger pin.
	digitalWrite(BACK_TRIGGER, LOW);
	delayMicroseconds(2);

	// Set the trigger pin on HIGH state for 10 micro seconds.
	digitalWrite(BACK_TRIGGER, HIGH);
	delayMicroseconds(10);
	digitalWrite(BACK_TRIGGER, LOW);

	// Read the echo pin.
	long duration = pulseIn(BACK_ECHO, HIGH); // Sound wave travel time in microseconds.

	backDistance = duration * SPEED_OF_SOUND / 2.0;
}

// Read the ultrasonic sensors.
void readUltrasonic() {
	readFrontUltrasonic();
	readBackUltrasonic();
}

void forward() {
	Serial.println("Forward");

	// Move forward.
	digitalWrite(LEFT_FORWARD, HIGH);
	digitalWrite(LEFT_BACKWARD, LOW);
	digitalWrite(RIGHT_FORWARD, HIGH);
	digitalWrite(RIGHT_BACKWARD, LOW);
}

void left() {
	Serial.println("Left");

	// Move left.
	digitalWrite(LEFT_FORWARD, LOW);
	digitalWrite(LEFT_BACKWARD, HIGH);
	digitalWrite(RIGHT_FORWARD, HIGH);
	digitalWrite(RIGHT_BACKWARD, LOW);
}

void right() {
	Serial.println("Right");

	// Move right.
	digitalWrite(LEFT_FORWARD, HIGH);
	digitalWrite(LEFT_BACKWARD, LOW);
	digitalWrite(RIGHT_FORWARD, LOW);
	digitalWrite(RIGHT_BACKWARD, HIGH);
}

void backward() {
	Serial.println("Backward");

	// Move forward.
	digitalWrite(LEFT_FORWARD, LOW);
	digitalWrite(LEFT_BACKWARD, HIGH);
	digitalWrite(RIGHT_FORWARD, LOW);
	digitalWrite(RIGHT_BACKWARD, HIGH);
}

void stop() {
	Serial.println("Stop");

	digitalWrite(LEFT_FORWARD, LOW);
	digitalWrite(LEFT_BACKWARD, LOW);

	digitalWrite(RIGHT_FORWARD, LOW);
	digitalWrite(RIGHT_BACKWARD, LOW);
}

// Check if a given LDR reading should trigger a reaction.
bool isLDRTriggered(int level) {
	return (level <= LDR_THRESHOLD);
}

// Check if any of the LDRs are triggered.
bool areLDRsTriggered() {
	return (isLDRTriggered(frontLeftLight) || isLDRTriggered(frontRightLight) || isLDRTriggered(backLeftLight) || isLDRTriggered(backRightLight));
}

// Move away from the edge.
// Return if we were touching the edge to begin with.
bool moveAwayFromEdge() {
	if (isLDRTriggered(frontLeftLight) && isLDRTriggered(frontRightLight)) {
		backward();
		return true;
	} else if (isLDRTriggered(backLeftLight) && isLDRTriggered(backRightLight)) {
		forward();
		return true;
	} else if (isLDRTriggered(frontLeftLight) && isLDRTriggered(backLeftLight)) {
		right();
		return true;
	} else if (isLDRTriggered(frontRightLight) && isLDRTriggered(backRightLight)) {
		left();
		return true;
	} else if (isLDRTriggered(frontLeftLight)) {
		right();
		return true;
	} else if (isLDRTriggered(frontRightLight)) {
		left();
		return true;
	} else if (isLDRTriggered(backLeftLight)) {
		right();
		return true;
	} else if (isLDRTriggered(backRightLight)) {
		left();
		return true;
	}
	return false;
}

void loop() {
	readLDR();
	readUltrasonic();

	if (!moveAwayFromEdge()) {
		if (frontDistance <= DISTANCE_THRESHOLD && frontDistance <= backDistance) {
			forward();
		} else if (backDistance <= DISTANCE_THRESHOLD && backDistance < frontDistance) {
			backward();
		} else {
			right();
		}
	}
}
